# Fritzing sketch Gikfun Auto H20 System (saved by Fritzing 0.9.3b)
breadboards: 1

parts:
  부품1 = FC-28 Soil Hygrometer Module - Probe
  부품3 = Arduino Uno (Rev3)
  부품2 = FC-28 Soil Hygrometer Module
  KY-1 = Keyes Relay [package=THT]
  VCC1 = 4 x AAA Battery Mount

nets:
  N1: 부품1.POS, 부품2.POS
  N2: 부품1.NEG, 부품2.NEG
  N3: 부품3.A0, 부품2.AO
  N4: 부품3.D5_PWM, KY-1.signal
  5V: 부품3.5V, 부품2.VCC, KY-1.power
  GND: 부품3.GND, 부품2.GND, KY-1.ground, VCC1.-
  N5: KY-1.C, VCC1.+

notes:
  The pins on the YL-38 are reversed. Check the sensor before wiring.
  PUMP

custom parts:
  FC-28 Soil Hygrometer Module - Probe: The FC-28 is a soil hygrometer module that uses the Texas Instruments LM393 comparator chip to provide an analog measurement of soil humidity.
  FC-28 Soil Hygrometer Module: The FC-28 is a soil hygrometer module that uses the Texas Instruments LM393 comparator chip to provide an analog measurement of soil humidity. The digital output is high when soil moisture is over a certain threshold, as determined by adjusting the potentiometer.
  Keyes Relay: The Keyes 5V relay module is suitable for SCM development, home appliance control. It uses a 5V~12V TIL control signal which can control DC / AC signal.
